# Fritzing sketch Schematic-Metereologic-Project (saved by Fritzing 1.0.4)
breadboards: 1

parts:
  Componente1 = Arduino Mega 2560 (Rev3)
  LCD1 = LCD screen
  microSD1 = MicroSD Card Module
  ZS-042_RTC1 = ZS-042 RTC Module
  Capacitive_Soil_Moisture_Sensor1 = DFRobot Capacitive Soil Moisture Sensor V1.0 [part_number=SEN0193]
  DS18B1 = DS18B20 1-Wire Temperature Sensor Module [part_number=DS18B20]
  LCM1602_IIC1 = LCM1602 IIC [part_number="LCM1602 IIC" chip_label="LCM1602 IIC" package="DIP (Dual Inline) [THT]"]
  R3 = Resistor [tolerance=±5% power=0.25W resistance=220 package=THT]
  M1 = BME280
  R2 = Resistor [tolerance=±5% power=0.25W resistance=220 package=THT]

nets:
  N1: Componente1.A9, M1.SDA
  N2: Componente1.A10, M1.SCL
  N3: Componente1.A11, ZS-042_RTC1.SDA
  N4: Componente1.A12, ZS-042_RTC1.SCL
  N5: Componente1.A13, LCM1602_IIC1.SDA
  N6: Componente1.A14, LCM1602_IIC1.SCL
  N7: Componente1.A15, Capacitive_Soil_Moisture_Sensor1.A
  GND: Componente1.GND, microSD1.GND, ZS-042_RTC1.GND, Capacitive_Soil_Moisture_Sensor1.GND, DS18B1.GND, LCM1602_IIC1.GND, R3.Pin_0, M1.GND
  N8: Componente1.D13_PWM, microSD1.SCK
  N9: Componente1.D12_PWM, microSD1.MISO
  N10: Componente1.D11_PWM, microSD1.MOSI
  N11: Componente1.D10_PWM, microSD1.CS
  N12: Componente1.D9_PWM, DS18B1.OUT, R3.Pin_1
  3V3: Componente1.3V3, M1.VIN
  VCC: Componente1.5V, microSD1.VCC, ZS-042_RTC1.VCC, Capacitive_Soil_Moisture_Sensor1.VCC, DS18B1.VDD, LCM1602_IIC1.VCC, R2.Pin_1
  VSS: LCD1.VSS, LCM1602_IIC1.VSS
  VDD: LCD1.VDD, LCM1602_IIC1.VDD
  N13: LCD1.V0, LCM1602_IIC1.V0
  N14: LCD1.RS, LCM1602_IIC1.RS
  N15: LCD1.R/W, LCM1602_IIC1.RW
  N16: LCD1.E, LCM1602_IIC1.E
  N17: LCD1.DB0, LCM1602_IIC1.D0
  N18: LCD1.DB1, LCM1602_IIC1.D1
  N19: LCD1.DB2, LCM1602_IIC1.D2
  N20: LCD1.DB3, LCM1602_IIC1.D3
  N21: LCD1.DB4, LCM1602_IIC1.D4
  N22: LCD1.DB5, LCM1602_IIC1.D5
  N23: LCD1.DB6, LCM1602_IIC1.D6
  N24: LCD1.DB7, LCM1602_IIC1.D7
  N25: LCD1.LED+, LCM1602_IIC1.A
  N26: LCD1.LED-, LCM1602_IIC1.K
  N27: LCM1602_IIC1.LED_A, LCM1602_IIC1.LED_B

custom parts:
  DFRobot Capacitive Soil Moisture Sensor V1.0: DFRobot Capacitive Soil Moisture Sensor V1.0 This product measures soil moisture levels by capacitive sensing, rather than resistive sensing like other types of moisture sensor. It is made of a corrosion resistant material giving it a long service life. Insert it into soil and impress your friends with the real-time soil moisture data! The product includes an on-board voltage regulator which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
  DS18B20 1-Wire Temperature Sensor Module: DS18B20 1-Wire Temperature Sensor Module The DS18B20 digital thermometer provides 9-bit to 12-bit Celsius temperature measurements and has an alarm function with nonvolatile user-programmable upper and lower trigger points. The DS18B20 communicates over a 1-Wire bus that by definition requires only one data line (and ground) for communication with a central microprocessor. In addition, the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
  LCM1602 IIC: I2C-Module to use a 1602 or 2004 LCD on with the wire.h libory Serial LCD Modul
  BME280: Temperature Humidity Barometric presure Sensor
